# Fritzing sketch HC05-Arduino (saved by Fritzing 0.9.3b)
circuit board: 8.46667cm x 5.64444cm

parts:
  HC-05 = Bluetooth HC-05 Macho
  Part4 = Arduino Uno (Rev3)

nets:
  RX_HC05: HC-05.TXD, Part4.D9_PWM
  TX_HC05: HC-05.RXD, Part4.D10_PWM/SS
  5V: HC-05.VCC, Part4.5V
  GND: HC-05.GND, Part4.GND

notes:
  IoT-Bluetooth, GIAO TIẾP GIỮA APP ANDROID VÀ ARDUINO THÔNG QUA MODULE BLUETOOTH, V1.0.0
